# Fritzing sketch Schematics 5 (saved by Fritzing 0.9.9b)
breadboards: 2

parts:
  Part1 = Arduino Nano (Rev3.0)
  IC1 = Voltage Regulator [package=to220-igo]
  LCD1 = LCD screen
  Mod1 = KY-019 5V Relay Module [package="Breakout board"]
  Q1 = NPN-Transistor [package="TO92 [THT]"]
  R1 = Resistor [tolerance=±5% resistance=220 package="0603 [SMD]"]
  Mod2 = KY-019 5V Relay Module [package="Breakout board"]
  Q2 = NPN-Transistor [package="TO92 [THT]"]
  R2 = Resistor [tolerance=±5% resistance=220 package="2010 [SMD]"]
  Mod3 = KY-019 5V Relay Module [package="Breakout board"]
  J1 = Peltier Element
  DHT1 = Humidity and Temperature Sensor DHT11
  R3 = Resistor [tolerance=±5% power=0.25 resistance=220 package=THT]
  Power_plug1 = Power plug
  R4 = Trimmer Potentiometer [maximum_resistance=10kΩ package=THT]
  F1 = Fan - Ventilador [package=THT]

nets:
  N1: Part1.GND, Q1.C, Mod2.-, Q2.E, DHT1.GND_2
  N2: Part1.D2, LCD1.DB7
  N3: Part1.D3, LCD1.DB6
  N4: Part1.D4, LCD1.DB5
  N5: Part1.D5, LCD1.DB4
  N6: Part1.D8, DHT1.Data-signal, R3.Pin_1
  N7: Part1.D9, R2.Pin_0
  N8: Part1.D10, R1.Pin_0
  N9: Part1.D11/MOSI, LCD1.E
  N10: Part1.D12/MISO, LCD1.RS
  N11: Part1.VIN, IC1.OUT
  N12: Part1.A0, R4.wiper
  GND: IC1.GND, Mod3.Common, Power_plug1.GND, F1.GND
  N13: IC1.IN, Mod1.Common, Power_plug1.VCC
  N14: LCD1.VSS, LCD1.R/W, LCD1.LED-
  VDD: LCD1.VDD, LCD1.LED+, Mod1.S, Mod1.+, Mod2.S, Mod2.+, Mod3.S, Mod3.+, DHT1.Vcc, R3.Pin_0, R4.leg1, R4.leg2
  N15: Mod1.-, Q1.E
  N16: Mod1.NO, Mod2.Common, F1.5V
  N17: Q1.B, R1.Pin_1
  N18: Mod2.NC, Mod3.NO, J1.pin2
  N19: Mod2.NO, Mod3.NC, J1.pin1
  N20: Q2.B, R2.Pin_1
  N21: Q2.C, Mod3.-

notes:
  POWER
  HOTCOLD
  -
  HOTCOLD
  +

custom parts:
  KY-019 5V Relay Module: KY-019 5V Relay module, used to control AC circuits. (Special thanks to vanepp for fixing the PCB holes and other errors)
  Humidity and Temperature Sensor DHT11: Digital relative humidity & temperature sensor DHT11
  Fan - Ventilador: Ventilador de 2 pines, se encuentra comunmente en computadoras de escritorio

// code stored in the sketch: Schematics.ino
/*
  REQUIRES the following Arduino libraries:
  - DHT Sensor Library: https://github.com/adafruit/DHT-sensor-library
  - Adafruit Unified Sensor Lib: https://github.com/adafruit/Adafruit_Sensor
  - LiquidCrystal.h
*/

#define DHTBOX_PIN 7                 // Digital pin connected to the DHT sensor (box)
#define DHTENV_PIN 8                 // Digital pin connected to the DHT sensor (enviroment
#define DHTTYPE DHT11                // DHT 11
#define POWER_PIN 10                 // Signal Pin of Relay for power
#define HOTCOLD_PIN 10               // Signal Pin of Relay for heather/cooler (polarization)
#define TRIMMER_PIN A0               // Signal from potentiometer (set)
#define TOLLERANCE 1.0                 // Tollerance for temperature set
#define DELAY_TIME 500

#include "DHT.h"
#include <LiquidCrystal.h>
DHT dht_box(DHTBOX_PIN, DHTTYPE);
DHT dht_env(DHTENV_PIN, DHTTYPE);

//Display
const int rs = 12, en = 11, d4 = 5, d5 = 4, d6 = 3, d7 = 2;
LiquidCrystal lcd(rs, en, d4, d5, d6, d7);
int count = 0;

//Buttons
int buttonState = 0;
float desiredTemperature = 0;

void setup() {
  Serial.begin(9600);
  pinMode(POWER_PIN, OUTPUT);
  pinMode(HOTCOLD_PIN, OUTPUT);
  dht_box.begin();
  dht_env.begin();
  lcd.begin(16, 2);
  lcd.print("DibeProofingBox");
  lcd.setCursor(0, 1);
  lcd.print("Version 0.2");
  delay(DELAY_TIME);
}

void loop() {
  count++;
  delay(DELAY_TIME);
  double t_box = dht_box.readTemperature();
  int h_box = dht_box.readHumidity();
  double t_env = dht_env.readTemperature();
  int h_env = dht_env.readHumidity();

  // Check if any reads failed and exit early (to try again).
  if (isnan(h_box) || isnan(t_box)) {
    Serial.println("Sensor BOX ERROR! ");
    lcd.setCursor(0, 0);
    lcd.print("Sensor BOX ERROR! ");
    lcd.setCursor(0, 1);
    lcd.print("                  ");
    return;
  }
  
  // Check if any reads failed and exit early (to try again).
  if (isnan(h_env) || isnan(t_env)) {
    Serial.println("Sensor ENV ERROR! ");
    lcd.setCursor(0, 0);
    lcd.print("Sensor ENV ERROR! ");
    lcd.setCursor(0, 1);
    lcd.print("                  ");
    return;
  }

  //Line 1
  char tF_box[6];
  dtostrf(t_box, 2, 1, tF_box);
  char tF_env[6];
  dtostrf(t_env, 2, 1, tF_env);
  String t_init = "";
  String line_1_a = t_init  + "Box: " + tF_box + (char)223 +" (" + h_box + "%)";
  String line_1_b = t_init  + "Env: " + tF_env + (char)223 +" (" + h_env + "%)";
  lcd.setCursor(0, 0);
  lcd.print(line_1_a);
  lcd.print(line_1_b);
  //Show the Environment temperature every now and then
  if (count > 20 && count <= 24) {  
    lcd.setCursor(0, 0);
    lcd.print(line_1_b);
    if (count >= 24) count = 0;
  }

  //Line 2
  Serial.println(line_1_a);
  lcd.setCursor(0, 1);
  int sensorValue = analogRead(TRIMMER_PIN);
  Serial.println(sensorValue);
  desiredTemperature = 0.025 * sensorValue + 7; //range between 7 and 32
  Serial.println(desiredTemperature);
  char tF_desidered[6];
  dtostrf(desiredTemperature, 2, 1, tF_desidered);
  String line_2 = t_init + "Desired: " + tF_desidered + (char)223;
  //lcd.print(line_2);


  if (t_box < desiredTemperature - TOLLERANCE || t_box > desiredTemperature + TOLLERANCE ) {
    Serial.println("Power enabled");
    digitalWrite(POWER_PIN, HIGH); 
    if (t_box < desiredTemperature - TOLLERANCE) {
      Serial.println("Heating");
      digitalWrite(HOTCOLD_PIN, HIGH); //heating
      line_2 += " H";
    }
    if (t_box > desiredTemperature - TOLLERANCE) {
      Serial.println("Cooling");
      digitalWrite(HOTCOLD_PIN, LOW); //cooling
      line_2 += " C";
    }
  }
  else {
    Serial.println("Maintaining");
    digitalWrite(POWER_PIN, LOW);
    digitalWrite(HOTCOLD_PIN, LOW);
    line_2 += " M";
  }
  lcd.print(line_2);
}
